# Fritzing sketch Base_PCB (saved by Fritzing 0.9.3b)
circuit board: 6.22776cm x 6.47267cm
breadboards: 1

parts:
  U1 = ESP32-38PinWide [part_number=ESP32-38PinWide]
  Servos = shrouded pin header, 10 pins [form="♂ (shrouded male)"]
  CAM_IF_Needed = male pin header, 2 pins [form="♂ (male)"]
  Motor_2_in = Screw terminal - 2 pins [package=THT]
  Motor_1_in = Screw terminal - 2 pins [package=THT]
  DC_motors = shrouded pin header, 10 pins [form="♂ (shrouded male)"]
  POWER_IN = Screw terminal - 2 pins [package=THT]
  J6 = female pin header, 19 pins [form="♀ (female)"]
  J8 = female pin header, 19 pins [form="♀ (female)"]

nets:
  N1: U1.3.3, DC_motors.pin8, J8.pin1
  N2: U1.EN, J8.pin2
  N3: U1.GPIO36, J8.pin3
  N4: U1.GPIO39, J8.pin4
  N5: U1.GPIO34, DC_motors.pin9, J8.pin5
  N6: U1.GPIO35, DC_motors.pin10, J8.pin6
  N7: U1.GPIO32, DC_motors.pin1, J8.pin7
  N8: U1.GPIO33, DC_motors.pin2, J8.pin8
  N9: U1.GPIO25, J8.pin9
  N10: U1.GPIO26, J8.pin10
  N11: U1.GPIO27, J8.pin11
  N12: U1.GPIO14, J8.pin12
  N13: U1.GPIO12, J8.pin13
  N14: U1.GND, Servos.pin2, Servos.pin9, DC_motors.pin3, POWER_IN.pin1, J6.pin1, J6.pin7, J8.pin14
  N15: U1.GPIO13, J8.pin15
  N16: U1.GPIO9, J8.pin16
  N17: U1.GPIO10, J8.pin17
  N18: U1.GPIO11, J8.pin18
  N19: U1.VIN, J8.pin19
  N20: U1.GPIO6, J6.pin19
  N21: U1.GPIO7, J6.pin18
  N22: U1.GPIO8, J6.pin17
  N23: U1.GPIO15, Servos.pin8, J6.pin16
  N24: U1.GPIO2, Servos.pin7, J6.pin15
  N25: U1.GPIO0, J6.pin14
  N26: U1.GPIO4, Servos.pin6, J6.pin13
  N27: U1.GPIO16, J6.pin12
  N28: U1.GPIO17, J6.pin11
  N29: U1.GPIO5, J6.pin10
  N30: U1.GPIO18, J6.pin9
  N31: U1.GPIO19, J6.pin8
  N32: U1.GPIO21, J6.pin6
  N33: U1.GPIO3, J6.pin5
  N34: U1.GPIO1, J6.pin4
  N35: U1.GPIO22, J6.pin3
  N36: U1.GPIO23, J6.pin2
  N37: Servos.pin1, Servos.pin10, POWER_IN.pin2
  N38: Servos.pin3, CAM_IF_Needed.pin1
  N39: Servos.pin4, CAM_IF_Needed.pin2
  N40: Motor_2_in.pin1, DC_motors.pin4
  N41: Motor_2_in.pin2, DC_motors.pin5
  N42: Motor_1_in.pin1, DC_motors.pin6
  N43: Motor_1_in.pin2, DC_motors.pin7

notes:
  M_-_1
  Encoder_B_1
  3.3
  GND
  Encoder_A_1
  M_+_1
  M_-_2
  M_+_2
  Encoder_B_2
  Encoder_A_2
  12V
  Servo_1
  Servo_2
  Servo_3
  CAM_COMM_1
  CAM_COMM_2
  IN_1
  IN_2
  IN_3
  IN_4
  EN_A
  EN_B

custom parts:
  ESP32-38PinWide: Generic 38-Pin ESP32 with wide format (only access to one side of pins on a breadboard) based on Stephen Lilley's HiLetgo ESP-WROOM-32 ESP32 ESP-32S Development Board.
