# Fritzing sketch Dc_PCB (saved by Fritzing 0.9.3b)
circuit board: 3.1cm x 2.9cm
breadboards: 1

parts:
  J1 = shrouded pin header, 10 pins [form="♂ (shrouded male)"]
  J3 = molex pin header, 6 pins [form=molex]
  J2 = molex pin header, 6 pins [form=molex]

nets:
  N1: J1.pin1, J3.pin5
  N2: J1.pin2, J3.pin4
  N3: J1.pin4, J3.pin2
  N4: J1.pin5, J3.pin1
  N5: J1.pin6, J2.pin6
  N6: J1.pin7, J2.pin5
  N7: J1.pin9, J2.pin2
  N8: J1.pin10, J2.pin1
  N9: J3.pin3, J2.pin4
  N10: J3.pin6, J2.pin3

notes:
  3.3
  GND
  Encoder_A_1
  Encoder_B_1
  M_+_1
  M_-_1
  M_-_2
  Encoder_B_2
  Encoder_A_2
  M_+_2
