# Fritzing sketch Servo_PCB (saved by Fritzing 0.9.3b)
circuit board: 5.25595cm x 2.07653cm
breadboards: 1

parts:
  J0 = shrouded pin header, 10 pins [form="♂ (shrouded male)"]
  S3 = female pin header, 3 pins [form="♀ (female)"]
  S2 = female pin header, 3 pins [form="♀ (female)"]
  S1 = female pin header, 3 pins [form="♀ (female)"]
  ESP = female pin header, 4 pins [form="♀ (female)"]
  V3_3 = Voltage Regulator - 3.3V [package="TO220 [THT]"]
  J11 = molex pin header, 2 pins [form=molex]

nets:
  N1: J0.pin2, ESP.pin4
  N2: J0.pin3, ESP.pin3
  N3: J0.pin4, J0.pin7, S3.pin1, S2.pin1, S1.pin1, ESP.pin1, V3_3.output_voltage, J11.pin2
  N4: J0.pin5, J0.pin6, S3.pin2, S2.pin2, S1.pin2, V3_3.input_voltage, J11.pin1
  N5: J0.pin8, S1.pin3
  N6: J0.pin9, S2.pin3
  N7: J0.pin10, S3.pin3
  N8: ESP.pin2, V3_3.GND

notes:
  Servo_3
  Servo_2
  5V
  GND
  CAM_COMM_1
  CAM_COMM_2
  Servo_1
  SIG
  3.3V
